# Fritzing sketch noduino_PCB (saved by Fritzing 0.8.7b)
circuit board: 2.23cm x 2.81819cm

parts:
  LM358 = LM 358 Dual Op-Amp [package="DIP8 [THT]"]
  10k = Resistor [tolerance=±5% resistance=10k package="0603 [SMD]"]
  10k_2 = Resistor [tolerance=±5% resistance=10k package="0603 [SMD]"]
  10k_3 = Resistor [tolerance=±5% resistance=10k package="0603 [SMD]"]
  10k_4 = Resistor [tolerance=±5% resistance=10k package="0603 [SMD]"]
  1uf = Ceramic Capacitor [capacitance=100nF package="0603 [SMD, multilayer]"]
  LEDb = LED - 3mm [color="Red (633nm)" package="3 mm [THT]"]
  1k = Resistor [tolerance=±5% resistance=1k package="0603 [SMD]"]
  1k_2 = Resistor [tolerance=±5% resistance=1k package="0603 [SMD]"]
  LEDa = LED - 3mm [color="Red (633nm)" package="3 mm [THT]"]
  gnd/5v = female pin header, 2 pins [form="♀ (female)"]
  gnd/B = female pin header, 2 pins [form="♀ (female)"]
  gnd/A = female pin header, 2 pins [form="♀ (female)"]
  audioIN = Audio Jack (TRS) 3.5mm [package="4Ucon 08780 [THT]"]
  J5 = rounded female pin header, 1 pin [form="♀ (female rounded)"]  # not connected
  J6 = rounded female pin header, 1 pin [form="♀ (female rounded)"]  # not connected

nets:
  N1: LM358.connector0, 1k_2.Pin_1, gnd/A.pin1
  N2: LM358.connector1, 10k_2.Pin_1, audioIN.Ring
  N3: LM358.connector2, 10k_4.Pin_0
  N4: LM358.connector3, 10k.Pin_0, 10k_2.Pin_0, 10k_3.Pin_1, 10k_4.Pin_1, 1uf.0, LEDb.cathode, LEDa.cathode, gnd/5v.pin2, gnd/B.pin2, gnd/A.pin2, audioIN.Sleeve
  N5: LM358.connector4, 10k_3.Pin_0
  N6: LM358.connector5, 10k.Pin_1, audioIN.Tip
  N7: LM358.connector6, 1k.Pin_1, gnd/B.pin1
  N8: LM358.connector7, 1uf.1, gnd/5v.pin1
  N9: LEDb.anode, 1k.Pin_0
  N10: 1k_2.Pin_0, LEDa.anode

notes:
  this file is for the pcb!
