# Fritzing sketch noduino_breadboard (saved by Fritzing 0.8.7b)
breadboards: 1

parts:
  M1 = DC Motor
  J2 = Generic male alternating header - 6 pins [form="♂ (male)" package=THT]
  R1 = Resistor [tolerance=±5% resistance=1k package=THT]
  R2 = Resistor [tolerance=±5% resistance=1k package=THT]
  Q1 = TRANSISTOR_NPN [package=to-92-ammo]
  Q2 = TRANSISTOR_NPN [package=to-92-ammo]
  JACK1 = 2.1mm Barrel Jack with Terminal Block
  JACK2 = 2.1mm Barrel Jack with Terminal Block
  NEOPIXEL1 = Neopixel Strip -- White (60/m)

nets:
  N1: M1.pin_1, JACK1.POS
  N2: M1.pin_2, Q1.C
  N3: J2.pin2, R2.Pin_1
  N4: J2.pin6, R1.Pin_0
  N5: R1.Pin_1, Q2.B
  N6: R2.Pin_0, Q1.B
  N7: Q1.E, Q2.E, JACK1.NEG, JACK2.NEG
  N8: Q2.C, NEOPIXEL1.GND
  N9: JACK2.POS, NEOPIXEL1.DO

notes:
  12V ou autre
  5V
  this file is for the breadboard!

custom parts:
  Generic male alternating header - 6 pins: Generic male alternating header
  Neopixel Strip -- White (60/m): Neopixel Strip, White, 60 pixels per meter.
