# Fritzing sketch noduino_schematic (saved by Fritzing 0.8.7b)
breadboards: 1

parts:
  LM358 = LM 358 Dual Op-Amp [package="DIP8 [THT]"]
  10k = Resistor [tolerance=±5% resistance=10k package="0603 [SMD]"]
  1uf = Ceramic Capacitor [capacitance=100nF package="0603 [SMD, multilayer]"]
  1k = Resistor [tolerance=±5% resistance=1k package="0603 [SMD]"]
  LEDb = LED - 3mm [color="Red (633nm)" package="3 mm [THT]"]
  5v_/_GND = female pin header, 2 pins [form="♀ (female)"]
  B_/_GND = female pin header, 2 pins [form="♀ (female)"]
  A_/_GND = female pin header, 2 pins [form="♀ (female)"]
  audioIN = Audio Jack (TRS) 3.5mm [package="4Ucon 08780 [THT]"]
  1k1 = Resistor [tolerance=±5% resistance=1k package="0603 [SMD]"]  # not connected
  LEDa = LED - 3mm [color="Red (633nm)" package="3 mm [THT]"]
  10k1 = Resistor [tolerance=±5% resistance=10k package="0603 [SMD]"]
  10k2 = Resistor [tolerance=±5% resistance=10k package="0603 [SMD]"]
  10k3 = Resistor [tolerance=±5% resistance=10k package="0603 [SMD]"]

nets:
  N1: LM358.connector0, A_/_GND.pin1
  N2: LM358.connector1, audioIN.Ring, 10k3.Pin_0
  N3: LM358.connector2, 10k1.Pin_0
  GND: LM358.connector3, 10k.Pin_0, 1uf.1, LEDb.cathode, 5v_/_GND.pin2, B_/_GND.pin2, A_/_GND.pin2, audioIN.Sleeve, LEDa.cathode, 10k2.Pin_0, 10k3.Pin_1
  N4: LM358.connector4, 10k.Pin_1
  N5: LM358.connector5, audioIN.Tip, 10k2.Pin_1
  N6: LM358.connector6, 1k.Pin_0, B_/_GND.pin1
  5V: LM358.connector7, 1uf.0, 5v_/_GND.pin1
  N7: 1k.Pin_1, LEDb.anode

notes:
  this file is for the schematic!
